# Fritzing sketch Veroboard (saved by Fritzing 0.9.3b)
stripboards: 1

parts:
  P5 = longpad pin header, 4 pins [form="long pad"]
  P3 = longpad pin header, 6 pins [form="long pad"]
  P4 = longpad pin header, 7 pins [form="long pad"]
  P1 = longpad pin header, 8 pins [form="long pad"]
  BT1 = longpad pin header, 2 pins [form="long pad"]
  P2 = longpad pin header, 10 pins [form="long pad"]
  P10 = longpad pin header, 3 pins [form="long pad"]
  P11 = longpad pin header, 3 pins [form="long pad"]
  P9 = longpad pin header, 3 pins [form="long pad"]
  P12 = longpad pin header, 3 pins [form="long pad"]
  P8 = longpad pin header, 3 pins [form="long pad"]
  SW1 = longpad pin header, 3 pins [form="long pad"]
  P6 = longpad pin header, 5 pins [form="long pad"]
  P7 = longpad pin header, 3 pins [form="long pad"]
  SW2 = DIP SWITCH [package=dipswitch-02]

nets:
  N1: P5.pin1, P4.pin2, P4.pin3, BT1.pin2, P10.pin1, P11.pin1, P9.pin1, P12.pin1, P8.pin1, SW1.pin1, P6.pin1, P7.pin1
  N2: P5.pin2, P4.pin4, P10.pin2, P11.pin2, P9.pin2, P12.pin2, P8.pin2, SW1.pin3, P6.pin2, P7.pin2, SW2.3, SW2.4
  N3: P5.pin3, P3.pin4
  N4: P5.pin4, P3.pin5
  N5: P3.pin1, P6.pin5
  N6: P3.pin2, P6.pin4
  N7: P3.pin3, P6.pin3
  N8: P4.pin1, BT1.pin1
  N9: P1.pin4, P7.pin3
  N10: P1.pin5, SW1.pin2
  N11: P1.pin6, P8.pin3
  N12: P1.pin7, P9.pin3
  N13: P1.pin8, SW2.2
  N14: P2.pin1, SW2.1
  N15: P2.pin2, P10.pin3
  N16: P2.pin3, P11.pin3
  N17: P2.pin4, P12.pin3

notes:
  5V
  GND
  12V
